// Logisim project Ctl_Shift_Add_Sub_Mov.circ as structural Verilog: 1 circuit, main circuit Shift_Add_Sub_Mov
module Shift_Add_Sub_Mov (
  input  Enable,
  input  [15:0] Instruction,
  output [3:0] Flags_Update_Mask,
  output Carry,
  output Imm32_Enable,
  output [3:0] ALU_Opcode,
  output [31:0] Imm32,
  output [4:0] Imm5,
  output [2:0] Rd,
  output [2:0] Rm,
  output [2:0] Rn
);

  wire and_1_out, and_2_out, and_3_out, not_1_out, not_2_out, not_3_out, not_4_out, not_5_out, not_6_out;
  wire [2:0] and_4_out, and_7_out, and_10_out, and_13_out;

  not not_1 (not_1_out, Instruction[13]);
  not not_2 (not_2_out, Instruction[14]);
  not not_3 (not_3_out, Instruction[15]);
  not not_4 (not_4_out, Instruction[10]);
  and and_1 (and_1_out, not_1_out, not_2_out, not_3_out);
  not not_5 (not_5_out, and_2_out);
  and and_2 (and_2_out, Instruction[11], Instruction[12], not_4_out);
  and and_3 (and_3_out, Instruction[11], Instruction[12]);
  and and_4 (and_4_out[0], Instruction[8], not_6_out);
  and and_5 (and_4_out[1], Instruction[9], not_6_out);
  and and_6 (and_4_out[2], Instruction[10], not_6_out);
  not not_6 (not_6_out, and_1_out);
  and and_7 (and_7_out[0], Instruction[0], and_1_out);
  and and_8 (and_7_out[1], Instruction[1], and_1_out);
  and and_9 (and_7_out[2], Instruction[2], and_1_out);
  and and_10 (and_10_out[0], Instruction[3], not_5_out);
  and and_11 (and_10_out[1], Instruction[4], not_5_out);
  and and_12 (and_10_out[2], Instruction[5], not_5_out);
  and and_13 (and_13_out[0], Instruction[6], and_2_out);
  and and_14 (and_13_out[1], Instruction[7], and_2_out);
  and and_15 (and_13_out[2], Instruction[8], and_2_out);
  and and_16 (Rn[0], Instruction[3], and_3_out);
  and and_17 (Rn[1], Instruction[4], and_3_out);
  and and_18 (Rn[2], Instruction[5], and_3_out);
  assign Rm = and_10_out | and_13_out;  // OR_Gate or_1, 3 bits wide
  assign Rd = and_4_out | and_7_out;  // OR_Gate or_2, 3 bits wide

  assign Imm5 = Instruction[10:6];
  assign Imm32 = {{24{1'b0}}, Instruction[7:0]};

  // Other names for the same wires on the sheet: Instru_8 = Instruction[8]; Instru_9 = Instruction[9];
  //   Instru_10 = Instruction[10]; Instru_0 = Instruction[0]; Instru_1 = Instruction[1]; Instru_2 = Instruction[2];
  //   Instru_3 = Instruction[3]; Instru_4 = Instruction[4]; Instru_5 = Instruction[5]; Instru_6 = Instruction[6];
  //   Instru_7 = Instruction[7]; Instru_11 = Instruction[11]; Instru_12 = Instruction[12];
  //   Instru_13 = Instruction[13]; Instru_14 = Instruction[14]; Instru_15 = Instruction[15]

  // Notes on the sheet:
  //   Pull output low on Enable = 0
  //   only ADD and SUB use Rm
  //   Enable carry for SUB since it is reversed in ALU
  //   ALU will use Imm32 instead of Rm
endmodule
